// Digital circuit Instruction Decoder.dig as structural Verilog
module Instruction_Decoder (
  input  CLK,
  input  I0,
  input  I1,
  input  I2,
  input  I3,
  input  I4,
  input  I5,
  input  I6,
  input  I7,
  input  IRQ,
  input  INT,
  input  F0,
  input  FC,
  input  FO,
  input  FN,
  output ALUE,
  output ALU_B,
  output ALUC,
  output ALUS,
  output ALUADD,
  output ALUAND,
  output ALUOR,
  output ALUNOT,
  output ALUXOR,
  output ALUSL,
  output ALUSR,
  output ALURL,
  output ALURR,
  output ALUMULT,
  output ALUDIV,
  output AR,
  output AW,
  output XR,
  output XW,
  output YR,
  output YW,
  output ZR,
  output ZW,
  output PCE,
  output PCHR,
  output PCHW,
  output PCLR,
  output PCLW,
  output SPR,
  output SPW,
  output SPINC,
  output SPDEC,
  output OHR,
  output OHW,
  output OLR,
  output OLW,
  output MAWL,
  output MAWH,
  output SCF,
  output CCF,
  output SIMF,
  output CIMF,
  output IRQO,
  output INTACK,
  output HLT,
  output MR,
  output MW
);

  wire flagregister_1_o0, flagsregister4b_1_o0, flagsregister4b_1_o1, flagsregister4b_1_o2,
       flagsregister4b_1_o3, interrupthandler_1_p11, not_1_out, not_2_out, undriven, undriven_2, undriven_3,
       undriven_4, undriven_5, undriven_6, undriven_7, undriven_8, undriven_9, undriven_10, undriven_11,
       undriven_12, undriven_13, undriven_14, undriven_15, undriven_16, undriven_17, undriven_18;
  wire [10:0] counter_1_out;
  wire [48:0] rom_1_d;
  wire [48:47] undriven_19;

  not not_1 (not_1_out, CLK);
  Counter #(.Bits(3)) counter_1 (
    .en(not_1_out), .C(not_1_out), .clr(undriven_19[47]), .out(counter_1_out[2:0]));  // open: ovf
  Register register_1 (
    .CLK(undriven_17), .E(1'b1), .R(1'b1), .W(undriven), .D0(I0), .D1(I1), .D2(I2), .D3(I3), .D4(I4),
    .D5(I5), .D6(I6), .D7(I7), .O0(counter_1_out[3]), .O1(counter_1_out[4]), .O2(counter_1_out[5]),
    .O3(counter_1_out[6]), .O4(counter_1_out[7]), .O5(counter_1_out[8]), .O6(counter_1_out[9]),
    .O7(counter_1_out[10]));
  FlagsRegister4b flagsregister4b_1 (
    .CLK(undriven_17), .F0(FC), .S0(undriven_16), .R0(undriven_15), .E0(undriven_14), .F1(FN),
    .S1(undriven_13), .R1(undriven_12), .E1(undriven_11), .F2(F0), .S2(undriven_10), .R2(undriven_9),
    .E2(undriven_8), .F3(FO), .S3(undriven_7), .R3(undriven_6), .E3(undriven_5), .O0(flagsregister4b_1_o0),
    .O1(flagsregister4b_1_o1), .O2(flagsregister4b_1_o2), .O3(flagsregister4b_1_o3));
  FlagRegister flagregister_1 (
    .CLK(undriven_17), .F0(1'b0), .S0(undriven_4), .R0(undriven_3), .E0(undriven_2), .O0(flagregister_1_o0));
  // InterruptHandler interrupthandler_1: pin names not known; wires that end beside it: flagsregister4b_1_o3, flagsregister4b_1_o2, flagsregister4b_1_o1, counter_1_out[0], counter_1_out[1], counter_1_out[2], flagsregister4b_1_o0, IRQ, INT, flagregister_1_o0, interrupthandler_1_p11
  ROM #(.AddrBits(10), .Bits(49)) rom_1 (.A(counter_1_out[9:0]), .sel(1'b1), .D(rom_1_d));
  assign ALUE = not_2_out ? rom_1_d[0] : 1'bz;  // Driver driver_1
  not not_2 (not_2_out, undriven_18);
  assign ALUE = undriven_18 ? interrupthandler_1_p11 : 1'bz;  // Driver driver_2
  // Pins of 10 and 11 bits meet at counter_1_out
  // Pins of 1 and 49 bits meet at rom_1_d
  // Pins of 1 and 49 bits meet at {undriven_19, HLT, INTACK, IRQO, CIMF, SIMF, CCF, SCF, MW, MR, MAWH, MAWL, OLW, OLR, OHW, OHR, SPDEC, SPINC, SPW, SPR, PCLW, PCLR, PCHW, PCHR, PCE, ZW, ZR, YW, YR, XW, XR, AW, AR, ALUDIV, ALUMULT, ALURR, ALURL, ALUSR, ALUSL, ALUXOR, ALUNOT, ALUOR, ALUAND, ALUADD, ALUS, ALUC, ALU_B, ALUE}
endmodule
