// Digital circuit InterruptHandler.dig as structural Verilog
module InterruptHandler (
  input  S0,
  input  S1,
  input  S2,
  input  INT,
  input  IRQ,
  input  IMF,
  output BLKINST
);

  wire and_1_out;
  wire [3:0] rom_1_d;

  and and_1 (and_1_out, IRQ, IMF);
  or or_1 (BLKINST, INT, and_1_out);
  ROM #(.AddrBits(3), .Bits(4)) rom_1 (.A({S2, S1, S0}), .sel(BLKINST), .D(rom_1_d));
endmodule
